// Logisim project TalosES_AL_card.circ as structural Verilog: 1 circuit, main circuit AL
module AL (
  input  AR2LE,
  input  AR2OE,
  input  CLK,
  input  nRST,
  input  AR1LE,
  input  AR1OE,
  input  AR1CE,
  input  AR2CE,
  input  [7:0] IBH,
  input  [7:0] IBL,
  input  PCLE,
  input  PCOE,
  input  JAHLE,
  input  JALLE,
  output [15:0] EAB,
  output [15:0] PC
);

  wire n7414_1_pin3, n7414_1_pin4, n7414_1_pin6, n7414_1_pin10, n7414_1_pin12, n7414_1_pin13, n7414_2_pin4,
       n7414_2_pin5, n7414_2_pin6, n7414_2_pin8, n7414_2_pin10, n7414_2_pin12, n7414_2_pin13, n74161_1_pin9,
       n74161_1_pin10, n74161_1_pin15, n74161_2_pin10, n74161_3_pin10, n74161_4_pin10, n74161_5_pin10,
       n74161_5_pin15, n74161_6_pin7, n74161_6_pin10, n74161_6_pin15, n74161_7_pin10, n74161_8_pin10,
       n74161_9_pin10, n74161_10_pin10, n74161_11_pin10, n74161_12_pin10, n74377_1_pin1;
  wire [3:0] n74161_5_pin14, n74161_6_pin14, n74377_1_pin2, n74377_1_pin12, n74377_2_pin2, n74377_2_pin12;
  wire [7:0] n74161_2_pin14, n74161_4_pin14;
  wire [11:0] n74161_11_pin14, n74161_12_pin14;

  // NoConnect on n74161_1_pin15
  _74161 u_74161_1 (
    .pin1(nRST), .pin2(CLK), .pin3(IBH[4]), .pin4(IBH[5]), .pin5(IBH[6]), .pin6(IBH[7]), .pin7(AR1CE),
    .pin15(n74161_1_pin15), .pin14(n74161_2_pin14[4]), .pin13(n74161_2_pin14[5]), .pin12(n74161_2_pin14[6]),
    .pin11(n74161_2_pin14[7]), .pin10(n74161_1_pin10), .pin9(n74161_1_pin9));
  _74377 u_74377_1 (
    .pin1(n74377_1_pin1), .pin2(n74377_1_pin2[0]), .pin3(IBH[0]), .pin4(IBH[1]), .pin5(n74377_1_pin2[1]),
    .pin6(n74377_1_pin2[2]), .pin7(IBH[2]), .pin8(IBH[3]), .pin9(n74377_1_pin2[3]),
    .pin19(n74377_1_pin12[3]), .pin18(IBH[7]), .pin17(IBH[6]), .pin16(n74377_1_pin12[2]),
    .pin15(n74377_1_pin12[1]), .pin14(IBH[5]), .pin13(IBH[4]), .pin12(n74377_1_pin12[0]), .pin11(CLK));
  _74161 u_74161_2 (
    .pin1(nRST), .pin2(CLK), .pin3(IBH[0]), .pin4(IBH[1]), .pin5(IBH[2]), .pin6(IBH[3]), .pin7(AR1CE),
    .pin15(n74161_1_pin10), .pin14(n74161_2_pin14[0]), .pin13(n74161_2_pin14[1]), .pin12(n74161_2_pin14[2]),
    .pin11(n74161_2_pin14[3]), .pin10(n74161_2_pin10), .pin9(n74161_1_pin9));
  _7414 u_7414_1 (
    .pin1(JAHLE), .pin2(n74377_1_pin1), .pin3(n7414_1_pin3), .pin4(n7414_1_pin4), .pin5(JALLE),
    .pin6(n7414_1_pin6), .pin13(n7414_1_pin13), .pin12(n7414_1_pin12), .pin11(PCOE), .pin10(n7414_1_pin10),
    .pin9(PCLE));  // open: pin8
  _74161 u_74161_3 (
    .pin1(nRST), .pin2(CLK), .pin3(IBL[4]), .pin4(IBL[5]), .pin5(IBL[6]), .pin6(IBL[7]), .pin7(AR1CE),
    .pin15(n74161_2_pin10), .pin14(n74161_4_pin14[4]), .pin13(n74161_4_pin14[5]), .pin12(n74161_4_pin14[6]),
    .pin11(n74161_4_pin14[7]), .pin10(n74161_3_pin10), .pin9(n74161_1_pin9));
  // NoConnect on n7414_1_pin12
  // NoConnect on n7414_1_pin4
  _74377 u_74377_2 (
    .pin1(n7414_1_pin6), .pin2(n74377_2_pin2[0]), .pin3(IBL[0]), .pin4(IBL[1]), .pin5(n74377_2_pin2[1]),
    .pin6(n74377_2_pin2[2]), .pin7(IBL[2]), .pin8(IBL[3]), .pin9(n74377_2_pin2[3]),
    .pin19(n74377_2_pin12[3]), .pin18(IBL[7]), .pin17(IBL[6]), .pin16(n74377_2_pin12[2]),
    .pin15(n74377_2_pin12[1]), .pin14(IBL[5]), .pin13(IBL[4]), .pin12(n74377_2_pin12[0]), .pin11(CLK));
  _74161 u_74161_4 (
    .pin1(nRST), .pin2(CLK), .pin3(IBL[0]), .pin4(IBL[1]), .pin5(IBL[2]), .pin6(IBL[3]), .pin7(AR1CE),
    .pin15(n74161_3_pin10), .pin14(n74161_4_pin14[0]), .pin13(n74161_4_pin14[1]), .pin12(n74161_4_pin14[2]),
    .pin11(n74161_4_pin14[3]), .pin10(n74161_4_pin10), .pin9(n74161_1_pin9));
  _7414 u_7414_2 (
    .pin1(AR1LE), .pin2(n74161_1_pin9), .pin3(AR1OE), .pin4(n7414_2_pin4), .pin5(n7414_2_pin5),
    .pin6(n7414_2_pin6), .pin13(n7414_2_pin13), .pin12(n7414_2_pin12), .pin11(AR2LE), .pin10(n7414_2_pin10),
    .pin9(AR2OE), .pin8(n7414_2_pin8));
  // NoConnect on n7414_2_pin12
  // NoConnect on n7414_2_pin6
  IC74245 ic74245_1 (
    .DIR(1'b0), .iOE(n7414_2_pin4), .B0(n74161_4_pin14[0]), .B1(n74161_4_pin14[1]), .B2(n74161_4_pin14[2]),
    .B3(n74161_4_pin14[3]), .B4(n74161_4_pin14[4]), .B5(n74161_4_pin14[5]), .B6(n74161_4_pin14[6]),
    .B7(n74161_4_pin14[7]), .A0(EAB[0]), .A1(EAB[1]), .A2(EAB[2]), .A3(EAB[3]), .A4(EAB[4]), .A5(EAB[5]),
    .A6(EAB[6]), .A7(EAB[7]));
  IC74245 ic74245_2 (
    .DIR(1'b0), .iOE(n7414_2_pin4), .B0(n74161_2_pin14[0]), .B1(n74161_2_pin14[1]), .B2(n74161_2_pin14[2]),
    .B3(n74161_2_pin14[3]), .B4(n74161_2_pin14[4]), .B5(n74161_2_pin14[5]), .B6(n74161_2_pin14[6]),
    .B7(n74161_2_pin14[7]), .A0(EAB[8]), .A1(EAB[9]), .A2(EAB[10]), .A3(EAB[11]), .A4(EAB[12]), .A5(EAB[13]),
    .A6(EAB[14]), .A7(EAB[15]));
  // NoConnect on n74161_5_pin15
  _74161 u_74161_5 (
    .pin1(nRST), .pin2(CLK), .pin3(IBH[4]), .pin4(IBH[5]), .pin5(IBH[6]), .pin6(IBH[7]), .pin7(AR2CE),
    .pin15(n74161_5_pin15), .pin14(n74161_5_pin14[0]), .pin13(n74161_5_pin14[1]), .pin12(n74161_5_pin14[2]),
    .pin11(n74161_5_pin14[3]), .pin10(n74161_5_pin10), .pin9(n7414_2_pin10));
  // NoConnect on n74161_6_pin15
  _74161 u_74161_6 (
    .pin1(nRST), .pin2(CLK), .pin3(n74377_1_pin12[0]), .pin4(n74377_1_pin12[1]), .pin5(n74377_1_pin12[2]),
    .pin6(n74377_1_pin12[3]), .pin7(n74161_6_pin7), .pin15(n74161_6_pin15), .pin14(n74161_6_pin14[0]),
    .pin13(n74161_6_pin14[1]), .pin12(n74161_6_pin14[2]), .pin11(n74161_6_pin14[3]), .pin10(n74161_6_pin10),
    .pin9(PCLE));
  _74161 u_74161_7 (
    .pin1(nRST), .pin2(CLK), .pin3(IBH[0]), .pin4(IBH[1]), .pin5(IBH[2]), .pin6(IBH[3]), .pin7(AR2CE),
    .pin15(n74161_5_pin10), .pin14(n74161_11_pin14[8]), .pin13(n74161_11_pin14[9]),
    .pin12(n74161_11_pin14[10]), .pin11(n74161_11_pin14[11]), .pin10(n74161_7_pin10), .pin9(n7414_2_pin10));
  _74161 u_74161_8 (
    .pin1(nRST), .pin2(CLK), .pin3(n74377_1_pin2[0]), .pin4(n74377_1_pin2[1]), .pin5(n74377_1_pin2[2]),
    .pin6(n74377_1_pin2[3]), .pin7(n74161_6_pin7), .pin15(n74161_6_pin10), .pin14(n74161_12_pin14[8]),
    .pin13(n74161_12_pin14[9]), .pin12(n74161_12_pin14[10]), .pin11(n74161_12_pin14[11]),
    .pin10(n74161_8_pin10), .pin9(PCLE));
  _74161 u_74161_9 (
    .pin1(nRST), .pin2(CLK), .pin3(IBL[4]), .pin4(IBL[5]), .pin5(IBL[6]), .pin6(IBL[7]), .pin7(AR2CE),
    .pin15(n74161_7_pin10), .pin14(n74161_11_pin14[4]), .pin13(n74161_11_pin14[5]),
    .pin12(n74161_11_pin14[6]), .pin11(n74161_11_pin14[7]), .pin10(n74161_9_pin10), .pin9(n7414_2_pin10));
  _74161 u_74161_10 (
    .pin1(nRST), .pin2(CLK), .pin3(n74377_2_pin12[0]), .pin4(n74377_2_pin12[1]), .pin5(n74377_2_pin12[2]),
    .pin6(n74377_2_pin12[3]), .pin7(n74161_6_pin7), .pin15(n74161_8_pin10), .pin14(n74161_12_pin14[4]),
    .pin13(n74161_12_pin14[5]), .pin12(n74161_12_pin14[6]), .pin11(n74161_12_pin14[7]),
    .pin10(n74161_10_pin10), .pin9(PCLE));
  _74161 u_74161_11 (
    .pin1(nRST), .pin2(CLK), .pin3(IBL[0]), .pin4(IBL[1]), .pin5(IBL[2]), .pin6(IBL[3]), .pin7(AR2CE),
    .pin15(n74161_9_pin10), .pin14(n74161_11_pin14[0]), .pin13(n74161_11_pin14[1]),
    .pin12(n74161_11_pin14[2]), .pin11(n74161_11_pin14[3]), .pin10(n74161_11_pin10), .pin9(n7414_2_pin10));
  _74161 u_74161_12 (
    .pin1(nRST), .pin2(CLK), .pin3(n74377_2_pin2[0]), .pin4(n74377_2_pin2[1]), .pin5(n74377_2_pin2[2]),
    .pin6(n74377_2_pin2[3]), .pin7(n74161_6_pin7), .pin15(n74161_10_pin10), .pin14(n74161_12_pin14[0]),
    .pin13(n74161_12_pin14[1]), .pin12(n74161_12_pin14[2]), .pin11(n74161_12_pin14[3]),
    .pin10(n74161_12_pin10), .pin9(PCLE));
  IC74245 ic74245_3 (
    .DIR(1'b0), .iOE(n7414_2_pin8), .B0(n74161_11_pin14[0]), .B1(n74161_11_pin14[1]),
    .B2(n74161_11_pin14[2]), .B3(n74161_11_pin14[3]), .B4(n74161_11_pin14[4]), .B5(n74161_11_pin14[5]),
    .B6(n74161_11_pin14[6]), .B7(n74161_11_pin14[7]), .A0(EAB[0]), .A1(EAB[1]), .A2(EAB[2]), .A3(EAB[3]),
    .A4(EAB[4]), .A5(EAB[5]), .A6(EAB[6]), .A7(EAB[7]));
  IC74245 ic74245_4 (
    .DIR(1'b0), .iOE(n7414_2_pin8), .B0(n74161_11_pin14[8]), .B1(n74161_11_pin14[9]),
    .B2(n74161_11_pin14[10]), .B3(n74161_11_pin14[11]), .B4(n74161_5_pin14[0]), .B5(n74161_5_pin14[1]),
    .B6(n74161_5_pin14[2]), .B7(n74161_5_pin14[3]), .A0(EAB[8]), .A1(EAB[9]), .A2(EAB[10]), .A3(EAB[11]),
    .A4(EAB[12]), .A5(EAB[13]), .A6(EAB[14]), .A7(EAB[15]));
  IC74245 ic74245_5 (
    .DIR(1'b0), .iOE(n7414_1_pin10), .B0(n74161_12_pin14[0]), .B1(n74161_12_pin14[1]),
    .B2(n74161_12_pin14[2]), .B3(n74161_12_pin14[3]), .B4(n74161_12_pin14[4]), .B5(n74161_12_pin14[5]),
    .B6(n74161_12_pin14[6]), .B7(n74161_12_pin14[7]), .A0(PC[0]), .A1(PC[1]), .A2(PC[2]), .A3(PC[3]),
    .A4(PC[4]), .A5(PC[5]), .A6(PC[6]), .A7(PC[7]));
  IC74245 ic74245_6 (
    .DIR(1'b0), .iOE(n7414_1_pin10), .B0(n74161_12_pin14[8]), .B1(n74161_12_pin14[9]),
    .B2(n74161_12_pin14[10]), .B3(n74161_12_pin14[11]), .B4(n74161_6_pin14[0]), .B5(n74161_6_pin14[1]),
    .B6(n74161_6_pin14[2]), .B7(n74161_6_pin14[3]), .A0(PC[8]), .A1(PC[9]), .A2(PC[10]), .A3(PC[11]),
    .A4(PC[12]), .A5(PC[13]), .A6(PC[14]), .A7(PC[15]));
  // also tied to GND on the sheet: {n7414_1_pin13, n7414_1_pin3, n7414_2_pin13, n7414_2_pin5}
  // also tied to VCC on the sheet: {n74161_4_pin10, n74161_12_pin10, n74161_6_pin7, n74161_11_pin10}

  // Notes on the sheet:
  //   AR1CE: pull=up
  //   IBH: pull=up
  //   IBL: pull=up
  //   AR2CE: pull=up
  //   PC: pull=up
  //   EAB: pull=up
  //   JAHLE: pull=up
  //   JALLE: pull=up
  //   PCLE: pull=up
  //   PCOE: pull=up
  //   CLK: pull=up
  //   nRST: pull=up
  //   AR2OE: pull=up
  //   AR1LE: pull=up
  //   AR1OE: pull=up
  //   AR2LE: pull=up
  //   JAH
  //   AR1
  //   JAL
  //   AR2
  //   PC
endmodule
