// Logisim project TalosES_ALU_card.circ as structural Verilog: 1 circuit, main circuit ALU
module ALU (
  input  [7:0] AHI,
  input  [7:0] BHI,
  input  [7:0] ALI,
  input  [7:0] BLI,
  input  RLOE,
  input  SFW,
  input  SNH,
  input  RHOE,
  input  SNL,
  input  CLK,
  input  nRST,
  output [7:0] IBHO,
  output [7:0] IBLO,
  output SFL,
  output ZFL,
  output CFH,
  output CFL,
  output SFH,
  output ZFH
);

  wire n7400_1_pin3, n7400_1_pin4, n7400_1_pin6, n7400_1_pin8, n7402_2_pin1, n7402_2_pin4, n7402_2_pin10,
       n7402_2_pin13, n7408_1_pin4, n7408_1_pin5, n7408_1_pin6, n7408_1_pin9, n7408_1_pin10, n7408_1_pin11,
       n7408_1_pin12, n7408_2_pin3, n7408_2_pin11, n7414_1_pin2, n7414_1_pin4, n7414_1_pin6, n7414_1_pin10,
       n7486_1_pin2, n74273_2_pin4, n74273_2_pin7, n74273_2_pin16, n74273_2_pin17, n74273_2_pin18,
       n74273_2_pin19, n74283_1_pin2, n74283_1_pin6, n74283_1_pin7, n74283_1_pin9, n74283_1_pin11,
       n74283_1_pin15, n74283_2_pin2, n74283_2_pin6, n74283_2_pin7, n74283_2_pin11, n74283_2_pin15,
       n74283_3_pin2, n74283_3_pin6, n74283_3_pin7, n74283_3_pin11, n74283_3_pin15, n74283_4_pin2,
       n74283_4_pin6, n74283_4_pin11, n74283_4_pin15;
  wire [7:0] n74273_1_pin2, n74273_3_pin2;
  wire [15:0] n7402_2_pin8;

  _74273 u_74273_1 (
    .pin1(nRST), .pin2(n74273_1_pin2[0]), .pin3(n7402_2_pin8[8]), .pin4(n7402_2_pin8[9]),
    .pin5(n74273_1_pin2[1]), .pin6(n74273_1_pin2[2]), .pin7(n7402_2_pin8[10]), .pin8(n7402_2_pin8[11]),
    .pin9(n74273_1_pin2[3]), .pin19(n74273_1_pin2[7]), .pin18(n7402_2_pin8[15]), .pin17(n7402_2_pin8[14]),
    .pin16(n74273_1_pin2[6]), .pin15(n74273_1_pin2[5]), .pin14(n7402_2_pin8[13]), .pin13(n7402_2_pin8[12]),
    .pin12(n74273_1_pin2[4]), .pin11(CLK));
  _74283 u_74283_1 (
    .pin1(n7402_2_pin8[13]), .pin2(n74283_1_pin2), .pin3(AHI[5]), .pin4(n7402_2_pin8[12]), .pin5(AHI[4]),
    .pin6(n74283_1_pin6), .pin7(n74283_1_pin7), .pin15(n74283_1_pin15), .pin14(AHI[6]),
    .pin13(n7402_2_pin8[14]), .pin12(AHI[7]), .pin11(n74283_1_pin11), .pin10(n7402_2_pin8[15]),
    .pin9(n74283_1_pin9));
  _7486 u_7486_1 (
    .pin1(BHI[4]), .pin2(n7486_1_pin2), .pin3(n74283_1_pin6), .pin4(BHI[5]), .pin5(n7486_1_pin2),
    .pin6(n74283_1_pin2), .pin13(n7486_1_pin2), .pin12(BHI[7]), .pin11(n74283_1_pin11), .pin10(n7486_1_pin2),
    .pin9(BHI[6]), .pin8(n74283_1_pin15));
  _74283 u_74283_2 (
    .pin1(n7402_2_pin8[9]), .pin2(n74283_2_pin2), .pin3(AHI[1]), .pin4(n7402_2_pin8[8]), .pin5(AHI[0]),
    .pin6(n74283_2_pin6), .pin7(n74283_2_pin7), .pin15(n74283_2_pin15), .pin14(AHI[2]),
    .pin13(n7402_2_pin8[10]), .pin12(AHI[3]), .pin11(n74283_2_pin11), .pin10(n7402_2_pin8[11]),
    .pin9(n74283_1_pin7));
  IC74245 ic74245_1 (
    .DIR(1'b0), .iOE(n7414_1_pin2), .B0(n74273_1_pin2[0]), .B1(n74273_1_pin2[1]), .B2(n74273_1_pin2[2]),
    .B3(n74273_1_pin2[3]), .B4(n74273_1_pin2[4]), .B5(n74273_1_pin2[5]), .B6(n74273_1_pin2[6]),
    .B7(n74273_1_pin2[7]), .A0(IBHO[0]), .A1(IBHO[1]), .A2(IBHO[2]), .A3(IBHO[3]), .A4(IBHO[4]),
    .A5(IBHO[5]), .A6(IBHO[6]), .A7(IBHO[7]));
  _7408 u_7408_1 (
    .pin4(n7408_1_pin4), .pin5(n7408_1_pin5), .pin6(n7408_1_pin6), .pin13(n7408_1_pin6),
    .pin12(n7408_1_pin12), .pin11(n7408_1_pin11), .pin10(n7408_1_pin10), .pin9(n7408_1_pin9),
    .pin8(n7408_1_pin12));  // open: pin1, pin2, pin3
  _7486 u_7486_2 (
    .pin1(BHI[0]), .pin2(n7486_1_pin2), .pin3(n74283_2_pin6), .pin4(BHI[1]), .pin5(n7486_1_pin2),
    .pin6(n74283_2_pin2), .pin13(n7486_1_pin2), .pin12(BHI[3]), .pin11(n74283_2_pin11), .pin10(n7486_1_pin2),
    .pin9(BHI[2]), .pin8(n74283_2_pin15));
  _7402 u_7402_1 (
    .pin1(n7408_1_pin5), .pin2(n7402_2_pin8[14]), .pin3(n7402_2_pin8[15]), .pin4(n7408_1_pin4),
    .pin5(n7402_2_pin8[13]), .pin6(n7402_2_pin8[12]), .pin13(n7408_1_pin10), .pin12(n7402_2_pin8[11]),
    .pin11(n7402_2_pin8[10]), .pin10(n7408_1_pin9), .pin9(n7402_2_pin8[9]), .pin8(n7402_2_pin8[8]));
  _74273 u_74273_2 (
    .pin1(nRST), .pin2(SFL), .pin3(n7402_2_pin8[7]), .pin4(n74273_2_pin4), .pin5(CFL), .pin6(ZFL),
    .pin7(n74273_2_pin7), .pin8(n7402_2_pin8[15]), .pin9(SFH), .pin19(n74273_2_pin19),
    .pin18(n74273_2_pin18), .pin17(n74273_2_pin17), .pin16(n74273_2_pin16), .pin15(ZFH),
    .pin14(n7408_1_pin11), .pin13(n74283_1_pin9), .pin12(CFH), .pin11(CLK));
  _7400 u_7400_1 (
    .pin1(n74273_2_pin4), .pin2(SFW), .pin3(n7400_1_pin3), .pin4(n7400_1_pin4), .pin5(n7486_1_pin2),
    .pin6(n7400_1_pin6), .pin13(n7400_1_pin3), .pin12(n7400_1_pin6), .pin11(n74283_2_pin7), .pin10(RLOE),
    .pin9(RLOE), .pin8(n7400_1_pin8));
  _7414 u_7414_1 (
    .pin1(RHOE), .pin2(n7414_1_pin2), .pin3(SNL), .pin4(n7414_1_pin4), .pin5(n7414_1_pin4),
    .pin6(n7414_1_pin6), .pin13(SFW), .pin12(n7400_1_pin4), .pin11(SNH), .pin10(n7414_1_pin10),
    .pin9(n7414_1_pin10), .pin8(n7486_1_pin2));
  // NoConnect on n74273_2_pin19
  // NoConnect on n74273_2_pin16
  _7402 u_7402_2 (
    .pin1(n7402_2_pin1), .pin2(n7402_2_pin8[7]), .pin3(n7402_2_pin8[6]), .pin4(n7402_2_pin4),
    .pin5(n7402_2_pin8[5]), .pin6(n7402_2_pin8[4]), .pin13(n7402_2_pin13), .pin12(n7402_2_pin8[3]),
    .pin11(n7402_2_pin8[2]), .pin10(n7402_2_pin10), .pin9(n7402_2_pin8[1]), .pin8(n7402_2_pin8[0]));
  _7408 u_7408_2 (
    .pin1(n7402_2_pin4), .pin2(n7402_2_pin1), .pin3(n7408_2_pin3), .pin13(n7402_2_pin10),
    .pin12(n7402_2_pin13), .pin11(n7408_2_pin11), .pin10(n7408_2_pin11), .pin9(n7408_2_pin3),
    .pin8(n74273_2_pin7));  // open: pin4, pin5, pin6
  _74283 u_74283_3 (
    .pin1(n7402_2_pin8[5]), .pin2(n74283_3_pin2), .pin3(ALI[5]), .pin4(n7402_2_pin8[4]), .pin5(ALI[4]),
    .pin6(n74283_3_pin6), .pin7(n74283_3_pin7), .pin15(n74283_3_pin15), .pin14(ALI[6]),
    .pin13(n7402_2_pin8[6]), .pin12(ALI[7]), .pin11(n74283_3_pin11), .pin10(n7402_2_pin8[7]),
    .pin9(n74273_2_pin4));
  _7486 u_7486_3 (
    .pin1(BLI[4]), .pin2(n7414_1_pin6), .pin3(n74283_3_pin6), .pin4(BLI[5]), .pin5(n7414_1_pin6),
    .pin6(n74283_3_pin2), .pin13(n7414_1_pin6), .pin12(BLI[7]), .pin11(n74283_3_pin11), .pin10(n7414_1_pin6),
    .pin9(BLI[6]), .pin8(n74283_3_pin15));
  _74283 u_74283_4 (
    .pin1(n7402_2_pin8[1]), .pin2(n74283_4_pin2), .pin3(ALI[1]), .pin4(n7402_2_pin8[0]), .pin5(ALI[0]),
    .pin6(n74283_4_pin6), .pin7(n7414_1_pin6), .pin15(n74283_4_pin15), .pin14(ALI[2]),
    .pin13(n7402_2_pin8[2]), .pin12(ALI[3]), .pin11(n74283_4_pin11), .pin10(n7402_2_pin8[3]),
    .pin9(n74283_3_pin7));
  _74273 u_74273_3 (
    .pin1(nRST), .pin2(n74273_3_pin2[0]), .pin3(n7402_2_pin8[0]), .pin4(n7402_2_pin8[1]),
    .pin5(n74273_3_pin2[1]), .pin6(n74273_3_pin2[2]), .pin7(n7402_2_pin8[2]), .pin8(n7402_2_pin8[3]),
    .pin9(n74273_3_pin2[3]), .pin19(n74273_3_pin2[7]), .pin18(n7402_2_pin8[7]), .pin17(n7402_2_pin8[6]),
    .pin16(n74273_3_pin2[6]), .pin15(n74273_3_pin2[5]), .pin14(n7402_2_pin8[5]), .pin13(n7402_2_pin8[4]),
    .pin12(n74273_3_pin2[4]), .pin11(CLK));
  _7486 u_7486_4 (
    .pin1(BLI[0]), .pin2(n7414_1_pin6), .pin3(n74283_4_pin6), .pin4(BLI[1]), .pin5(n7414_1_pin6),
    .pin6(n74283_4_pin2), .pin13(n7414_1_pin6), .pin12(BLI[3]), .pin11(n74283_4_pin11), .pin10(n7414_1_pin6),
    .pin9(BLI[2]), .pin8(n74283_4_pin15));
  IC74245 ic74245_2 (
    .DIR(1'b0), .iOE(n7400_1_pin8), .B0(n74273_3_pin2[0]), .B1(n74273_3_pin2[1]), .B2(n74273_3_pin2[2]),
    .B3(n74273_3_pin2[3]), .B4(n74273_3_pin2[4]), .B5(n74273_3_pin2[5]), .B6(n74273_3_pin2[6]),
    .B7(n74273_3_pin2[7]), .A0(IBLO[0]), .A1(IBLO[1]), .A2(IBLO[2]), .A3(IBLO[3]), .A4(IBLO[4]),
    .A5(IBLO[5]), .A6(IBLO[6]), .A7(IBLO[7]));
  // also tied to GND on the sheet: {n74273_2_pin18, n74273_2_pin17}

  // Notes on the sheet:
  //   SFW: pull=up
  //   SNH: pull=up
  //   RHOE: pull=up
  //   SFL: pull=up
  //   CFL: pull=up
  //   ZFL: pull=up
  //   SFH: pull=up
  //   CFH: pull=up
  //   ZFH: pull=up
  //   RLOE: pull=up
  //   SNL: pull=up
  //   ALI: pull=up
  //   BLI: pull=up
  //   CLK: pull=up
  //   nRST: pull=up
  //   IBLO: pull=up
  //   AHI: pull=up
  //   BHI: pull=up
  //   IBHO: pull=up
  //   AH
  //   RH
  //   BH
  //   FR
  //   AL
  //   BL
  //   RL
endmodule
