// Logisim project TalosES_ALU_testbed.circ as structural Verilog: 1 circuit, main circuit ALU
module ALU (
  input  Standalone,
  input  [7:0] AHI,
  input  [7:0] BHI,
  input  [7:0] ALI,
  input  [7:0] BLI,
  input  nRST,
  input  RLOE,
  input  SFW,
  input  SNH,
  input  RHOE,
  input  SNL,
  output [7:0] IBHO,
  output [7:0] IBLO,
  output SFL,
  output ZFL,
  output CFH,
  output CFL,
  output SFH,
  output ZFH
);

  wire CLK, n7400_1_pin1, n7400_1_pin3, n7400_1_pin4, n7400_1_pin6, n7400_1_pin8, n7402_2_pin1, n7402_2_pin4,
       n7402_2_pin10, n7402_2_pin13, n7408_1_pin1, n7408_1_pin2, n7408_1_pin3, n7408_1_pin4, n7408_1_pin5,
       n7408_1_pin6, n7408_1_pin9, n7408_1_pin10, n7408_1_pin11, n7408_1_pin12, n7408_2_pin3, n7408_2_pin4,
       n7408_2_pin5, n7408_2_pin6, n7408_2_pin11, n7414_1_pin2, n7414_1_pin4, n7414_1_pin6, n7414_1_pin8,
       n7414_1_pin10, n7414_1_pin12, n7414_2_pin2, n7414_2_pin4, n7414_2_pin6, n7414_2_pin10, n7486_1_pin2,
       n74273_2_pin7, n74273_2_pin16, n74273_2_pin17, n74273_2_pin18, n74273_2_pin19, n74283_1_pin2,
       n74283_1_pin6, n74283_1_pin7, n74283_1_pin9, n74283_1_pin11, n74283_1_pin15, n74283_2_pin2,
       n74283_2_pin6, n74283_2_pin7, n74283_2_pin11, n74283_2_pin15, n74283_3_pin2, n74283_3_pin6,
       n74283_3_pin7, n74283_3_pin11, n74283_3_pin15, n74283_4_pin2, n74283_4_pin6, n74283_4_pin11,
       n74283_4_pin15;
  wire [7:0] ic74245_1_a0, ic74245_2_a0, ic74245_4_a0, ic74245_5_a0, ic74245_8_a0, ic74245_9_a0,
       ic74245_10_a0, ic74245_12_a0, ic74245_14_a0, ic74245_15_a0, n74273_1_pin2, n74273_3_pin2, undriven,
       undriven_2, undriven_3, undriven_4;
  wire [15:0] n7402_2_pin8;

  // DipSwitch dipswitch_1: pin names not known
  LedBar ledbar_1 (
    .led0(ic74245_2_a0[7]), .led1(ic74245_2_a0[6]), .led2(ic74245_2_a0[5]), .led3(ic74245_2_a0[4]),
    .led4(ic74245_2_a0[3]), .led5(ic74245_2_a0[2]), .led6(ic74245_2_a0[1]), .led7(ic74245_2_a0[0]));
  IC74245 ic74245_1 (
    .DIR(1'b0), .iOE(n7414_1_pin6), .B0(undriven[0]), .B1(undriven[1]), .B2(undriven[2]), .B3(undriven[3]),
    .B4(undriven[4]), .B5(undriven[5]), .B6(undriven[6]), .B7(undriven[7]), .A0(ic74245_1_a0[0]),
    .A1(ic74245_1_a0[1]), .A2(ic74245_1_a0[2]), .A3(ic74245_1_a0[3]), .A4(ic74245_1_a0[4]),
    .A5(ic74245_1_a0[5]), .A6(ic74245_1_a0[6]), .A7(ic74245_1_a0[7]));
  IC74245 ic74245_2 (
    .DIR(1'b0), .iOE(1'b0), .B0(ic74245_1_a0[0]), .B1(ic74245_1_a0[1]), .B2(ic74245_1_a0[2]),
    .B3(ic74245_1_a0[3]), .B4(ic74245_1_a0[4]), .B5(ic74245_1_a0[5]), .B6(ic74245_1_a0[6]),
    .B7(ic74245_1_a0[7]), .A0(ic74245_2_a0[0]), .A1(ic74245_2_a0[1]), .A2(ic74245_2_a0[2]),
    .A3(ic74245_2_a0[3]), .A4(ic74245_2_a0[4]), .A5(ic74245_2_a0[5]), .A6(ic74245_2_a0[6]),
    .A7(ic74245_2_a0[7]));
  _74273 u_74273_1 (
    .pin1(nRST), .pin2(n74273_1_pin2[0]), .pin3(n7402_2_pin8[8]), .pin4(n7402_2_pin8[9]),
    .pin5(n74273_1_pin2[1]), .pin6(n74273_1_pin2[2]), .pin7(n7402_2_pin8[10]), .pin8(n7402_2_pin8[11]),
    .pin9(n74273_1_pin2[3]), .pin19(n74273_1_pin2[7]), .pin18(n7402_2_pin8[15]), .pin17(n7402_2_pin8[14]),
    .pin16(n74273_1_pin2[6]), .pin15(n74273_1_pin2[5]), .pin14(n7402_2_pin8[13]), .pin13(n7402_2_pin8[12]),
    .pin12(n74273_1_pin2[4]), .pin11(CLK));
  IC74245 ic74245_3 (
    .DIR(1'b0), .iOE(n7414_1_pin4), .B0(AHI[0]), .B1(AHI[1]), .B2(AHI[2]), .B3(AHI[3]), .B4(AHI[4]),
    .B5(AHI[5]), .B6(AHI[6]), .B7(AHI[7]), .A0(ic74245_1_a0[0]), .A1(ic74245_1_a0[1]), .A2(ic74245_1_a0[2]),
    .A3(ic74245_1_a0[3]), .A4(ic74245_1_a0[4]), .A5(ic74245_1_a0[5]), .A6(ic74245_1_a0[6]),
    .A7(ic74245_1_a0[7]));
  _74283 u_74283_1 (
    .pin1(n7402_2_pin8[13]), .pin2(n74283_1_pin2), .pin3(ic74245_1_a0[5]), .pin4(n7402_2_pin8[12]),
    .pin5(ic74245_1_a0[4]), .pin6(n74283_1_pin6), .pin7(n74283_1_pin7), .pin15(n74283_1_pin15),
    .pin14(ic74245_1_a0[6]), .pin13(n7402_2_pin8[14]), .pin12(ic74245_1_a0[7]), .pin11(n74283_1_pin11),
    .pin10(n7402_2_pin8[15]), .pin9(n74283_1_pin9));
  LedBar ledbar_2 (
    .led0(ic74245_4_a0[7]), .led1(ic74245_4_a0[6]), .led2(ic74245_4_a0[5]), .led3(ic74245_4_a0[4]),
    .led4(ic74245_4_a0[3]), .led5(ic74245_4_a0[2]), .led6(ic74245_4_a0[1]), .led7(ic74245_4_a0[0]));
  // DipSwitch dipswitch_2: pin names not known
  IC74245 ic74245_4 (
    .DIR(1'b0), .iOE(1'b0), .B0(n74273_1_pin2[0]), .B1(n74273_1_pin2[1]), .B2(n74273_1_pin2[2]),
    .B3(n74273_1_pin2[3]), .B4(n74273_1_pin2[4]), .B5(n74273_1_pin2[5]), .B6(n74273_1_pin2[6]),
    .B7(n74273_1_pin2[7]), .A0(ic74245_4_a0[0]), .A1(ic74245_4_a0[1]), .A2(ic74245_4_a0[2]),
    .A3(ic74245_4_a0[3]), .A4(ic74245_4_a0[4]), .A5(ic74245_4_a0[5]), .A6(ic74245_4_a0[6]),
    .A7(ic74245_4_a0[7]));
  IC74245 ic74245_5 (
    .DIR(1'b0), .iOE(n7414_1_pin6), .B0(undriven_2[0]), .B1(undriven_2[1]), .B2(undriven_2[2]),
    .B3(undriven_2[3]), .B4(undriven_2[4]), .B5(undriven_2[5]), .B6(undriven_2[6]), .B7(undriven_2[7]),
    .A0(ic74245_5_a0[0]), .A1(ic74245_5_a0[1]), .A2(ic74245_5_a0[2]), .A3(ic74245_5_a0[3]),
    .A4(ic74245_5_a0[4]), .A5(ic74245_5_a0[5]), .A6(ic74245_5_a0[6]), .A7(ic74245_5_a0[7]));
  _7486 u_7486_1 (
    .pin1(ic74245_5_a0[4]), .pin2(n7486_1_pin2), .pin3(n74283_1_pin6), .pin4(ic74245_5_a0[5]),
    .pin5(n7486_1_pin2), .pin6(n74283_1_pin2), .pin13(n7486_1_pin2), .pin12(ic74245_5_a0[7]),
    .pin11(n74283_1_pin11), .pin10(n7486_1_pin2), .pin9(ic74245_5_a0[6]), .pin8(n74283_1_pin15));
  _74283 u_74283_2 (
    .pin1(n7402_2_pin8[9]), .pin2(n74283_2_pin2), .pin3(ic74245_1_a0[1]), .pin4(n7402_2_pin8[8]),
    .pin5(ic74245_1_a0[0]), .pin6(n74283_2_pin6), .pin7(n74283_2_pin7), .pin15(n74283_2_pin15),
    .pin14(ic74245_1_a0[2]), .pin13(n7402_2_pin8[10]), .pin12(ic74245_1_a0[3]), .pin11(n74283_2_pin11),
    .pin10(n7402_2_pin8[11]), .pin9(n74283_1_pin7));
  _7408 u_7408_1 (
    .pin1(n7408_1_pin1), .pin2(n7408_1_pin2), .pin3(n7408_1_pin3), .pin4(n7408_1_pin4), .pin5(n7408_1_pin5),
    .pin6(n7408_1_pin6), .pin13(n7408_1_pin6), .pin12(n7408_1_pin12), .pin11(n7408_1_pin11),
    .pin10(n7408_1_pin10), .pin9(n7408_1_pin9), .pin8(n7408_1_pin12));
  IC74245 ic74245_6 (
    .DIR(1'b0), .iOE(n7414_2_pin2), .B0(n74273_1_pin2[0]), .B1(n74273_1_pin2[1]), .B2(n74273_1_pin2[2]),
    .B3(n74273_1_pin2[3]), .B4(n74273_1_pin2[4]), .B5(n74273_1_pin2[5]), .B6(n74273_1_pin2[6]),
    .B7(n74273_1_pin2[7]), .A0(IBHO[0]), .A1(IBHO[1]), .A2(IBHO[2]), .A3(IBHO[3]), .A4(IBHO[4]),
    .A5(IBHO[5]), .A6(IBHO[6]), .A7(IBHO[7]));
  // NoConnect on n7408_1_pin3
  IC74245 ic74245_7 (
    .DIR(1'b0), .iOE(n7414_1_pin4), .B0(BHI[0]), .B1(BHI[1]), .B2(BHI[2]), .B3(BHI[3]), .B4(BHI[4]),
    .B5(BHI[5]), .B6(BHI[6]), .B7(BHI[7]), .A0(ic74245_5_a0[0]), .A1(ic74245_5_a0[1]), .A2(ic74245_5_a0[2]),
    .A3(ic74245_5_a0[3]), .A4(ic74245_5_a0[4]), .A5(ic74245_5_a0[5]), .A6(ic74245_5_a0[6]),
    .A7(ic74245_5_a0[7]));
  LedBar ledbar_3 (
    .led0(ic74245_8_a0[7]), .led1(ic74245_8_a0[6]), .led2(ic74245_8_a0[5]), .led3(ic74245_8_a0[4]),
    .led4(ic74245_8_a0[3]), .led5(ic74245_8_a0[2]), .led6(ic74245_8_a0[1]), .led7(ic74245_8_a0[0]));
  _7486 u_7486_2 (
    .pin1(ic74245_5_a0[0]), .pin2(n7486_1_pin2), .pin3(n74283_2_pin6), .pin4(ic74245_5_a0[1]),
    .pin5(n7486_1_pin2), .pin6(n74283_2_pin2), .pin13(n7486_1_pin2), .pin12(ic74245_5_a0[3]),
    .pin11(n74283_2_pin11), .pin10(n7486_1_pin2), .pin9(ic74245_5_a0[2]), .pin8(n74283_2_pin15));
  IC74245 ic74245_8 (
    .DIR(1'b0), .iOE(1'b0), .B0(ic74245_5_a0[0]), .B1(ic74245_5_a0[1]), .B2(ic74245_5_a0[2]),
    .B3(ic74245_5_a0[3]), .B4(ic74245_5_a0[4]), .B5(ic74245_5_a0[5]), .B6(ic74245_5_a0[6]),
    .B7(ic74245_5_a0[7]), .A0(ic74245_8_a0[0]), .A1(ic74245_8_a0[1]), .A2(ic74245_8_a0[2]),
    .A3(ic74245_8_a0[3]), .A4(ic74245_8_a0[4]), .A5(ic74245_8_a0[5]), .A6(ic74245_8_a0[6]),
    .A7(ic74245_8_a0[7]));
  _7402 u_7402_1 (
    .pin1(n7408_1_pin5), .pin2(n7402_2_pin8[15]), .pin3(n7402_2_pin8[14]), .pin4(n7408_1_pin4),
    .pin5(n7402_2_pin8[13]), .pin6(n7402_2_pin8[12]), .pin13(n7408_1_pin10), .pin12(n7402_2_pin8[11]),
    .pin11(n7402_2_pin8[10]), .pin10(n7408_1_pin9), .pin9(n7402_2_pin8[9]), .pin8(n7402_2_pin8[8]));
  _7414 u_7414_1 (
    .pin1(Standalone), .pin2(n7414_1_pin2), .pin3(n7414_1_pin2), .pin4(n7414_1_pin4), .pin5(n7414_1_pin4),
    .pin6(n7414_1_pin6), .pin13(Standalone), .pin12(n7414_1_pin12), .pin11(n7414_1_pin12),
    .pin10(n7414_1_pin10), .pin9(n7414_1_pin10), .pin8(n7414_1_pin8));
  Clock clock_1 (.out(CLK));
  _7400 u_7400_1 (
    .pin1(n7400_1_pin1), .pin2(SFW), .pin3(n7400_1_pin3), .pin4(n7400_1_pin4), .pin5(n7486_1_pin2),
    .pin6(n7400_1_pin6), .pin13(n7400_1_pin3), .pin12(n7400_1_pin6), .pin11(n74283_2_pin7), .pin10(RLOE),
    .pin9(RLOE), .pin8(n7400_1_pin8));
  _7414 u_7414_2 (
    .pin1(RHOE), .pin2(n7414_2_pin2), .pin3(SNL), .pin4(n7414_2_pin4), .pin5(n7414_2_pin4),
    .pin6(n7414_2_pin6), .pin13(SFW), .pin12(n7400_1_pin4), .pin11(SNH), .pin10(n7414_2_pin10),
    .pin9(n7414_2_pin10), .pin8(n7486_1_pin2));
  // NoConnect on n74273_2_pin19
  _74273 u_74273_2 (
    .pin1(nRST), .pin2(SFL), .pin3(n7402_2_pin8[7]), .pin4(n7400_1_pin1), .pin5(CFL), .pin6(ZFL),
    .pin7(n74273_2_pin7), .pin8(n7402_2_pin8[15]), .pin9(SFH), .pin19(n74273_2_pin19),
    .pin18(n74273_2_pin18), .pin17(n74273_2_pin17), .pin16(n74273_2_pin16), .pin15(ZFH),
    .pin14(n7408_1_pin11), .pin13(n74283_1_pin9), .pin12(CFH), .pin11(CLK));
  LED led_1 (.in(SFL));
  _7402 u_7402_2 (
    .pin1(n7402_2_pin1), .pin2(n7402_2_pin8[7]), .pin3(n7402_2_pin8[6]), .pin4(n7402_2_pin4),
    .pin5(n7402_2_pin8[5]), .pin6(n7402_2_pin8[4]), .pin13(n7402_2_pin13), .pin12(n7402_2_pin8[3]),
    .pin11(n7402_2_pin8[2]), .pin10(n7402_2_pin10), .pin9(n7402_2_pin8[1]), .pin8(n7402_2_pin8[0]));
  // NoConnect on n74273_2_pin16
  LED led_2 (.in(ZFL));
  LED led_3 (.in(CFL));
  LED led_4 (.in(SFH));
  LED led_5 (.in(CFH));
  LED led_6 (.in(ZFH));
  LedBar ledbar_4 (
    .led0(ic74245_10_a0[7]), .led1(ic74245_10_a0[6]), .led2(ic74245_10_a0[5]), .led3(ic74245_10_a0[4]),
    .led4(ic74245_10_a0[3]), .led5(ic74245_10_a0[2]), .led6(ic74245_10_a0[1]), .led7(ic74245_10_a0[0]));
  // DipSwitch dipswitch_3: pin names not known
  IC74245 ic74245_9 (
    .DIR(1'b0), .iOE(n7414_1_pin8), .B0(undriven_3[0]), .B1(undriven_3[1]), .B2(undriven_3[2]),
    .B3(undriven_3[3]), .B4(undriven_3[4]), .B5(undriven_3[5]), .B6(undriven_3[6]), .B7(undriven_3[7]),
    .A0(ic74245_9_a0[0]), .A1(ic74245_9_a0[1]), .A2(ic74245_9_a0[2]), .A3(ic74245_9_a0[3]),
    .A4(ic74245_9_a0[4]), .A5(ic74245_9_a0[5]), .A6(ic74245_9_a0[6]), .A7(ic74245_9_a0[7]));
  IC74245 ic74245_10 (
    .DIR(1'b0), .iOE(1'b0), .B0(ic74245_9_a0[0]), .B1(ic74245_9_a0[1]), .B2(ic74245_9_a0[2]),
    .B3(ic74245_9_a0[3]), .B4(ic74245_9_a0[4]), .B5(ic74245_9_a0[5]), .B6(ic74245_9_a0[6]),
    .B7(ic74245_9_a0[7]), .A0(ic74245_10_a0[0]), .A1(ic74245_10_a0[1]), .A2(ic74245_10_a0[2]),
    .A3(ic74245_10_a0[3]), .A4(ic74245_10_a0[4]), .A5(ic74245_10_a0[5]), .A6(ic74245_10_a0[6]),
    .A7(ic74245_10_a0[7]));
  _7408 u_7408_2 (
    .pin1(n7402_2_pin4), .pin2(n7402_2_pin1), .pin3(n7408_2_pin3), .pin4(n7408_2_pin4), .pin5(n7408_2_pin5),
    .pin6(n7408_2_pin6), .pin13(n7402_2_pin10), .pin12(n7402_2_pin13), .pin11(n7408_2_pin11),
    .pin10(n7408_2_pin11), .pin9(n7408_2_pin3), .pin8(n74273_2_pin7));
  // NoConnect on n7408_2_pin6
  IC74245 ic74245_11 (
    .DIR(1'b0), .iOE(n7414_1_pin10), .B0(ALI[0]), .B1(ALI[1]), .B2(ALI[2]), .B3(ALI[3]), .B4(ALI[4]),
    .B5(ALI[5]), .B6(ALI[6]), .B7(ALI[7]), .A0(ic74245_9_a0[0]), .A1(ic74245_9_a0[1]), .A2(ic74245_9_a0[2]),
    .A3(ic74245_9_a0[3]), .A4(ic74245_9_a0[4]), .A5(ic74245_9_a0[5]), .A6(ic74245_9_a0[6]),
    .A7(ic74245_9_a0[7]));
  _74283 u_74283_3 (
    .pin1(n7402_2_pin8[5]), .pin2(n74283_3_pin2), .pin3(ic74245_9_a0[5]), .pin4(n7402_2_pin8[4]),
    .pin5(ic74245_9_a0[4]), .pin6(n74283_3_pin6), .pin7(n74283_3_pin7), .pin15(n74283_3_pin15),
    .pin14(ic74245_9_a0[6]), .pin13(n7402_2_pin8[6]), .pin12(ic74245_9_a0[7]), .pin11(n74283_3_pin11),
    .pin10(n7402_2_pin8[7]), .pin9(n7400_1_pin1));
  // DipSwitch dipswitch_4: pin names not known
  _74273 u_74273_3 (
    .pin1(nRST), .pin2(n74273_3_pin2[0]), .pin3(n7402_2_pin8[0]), .pin4(n7402_2_pin8[1]),
    .pin5(n74273_3_pin2[1]), .pin6(n74273_3_pin2[2]), .pin7(n7402_2_pin8[2]), .pin8(n7402_2_pin8[3]),
    .pin9(n74273_3_pin2[3]), .pin19(n74273_3_pin2[7]), .pin18(n7402_2_pin8[7]), .pin17(n7402_2_pin8[6]),
    .pin16(n74273_3_pin2[6]), .pin15(n74273_3_pin2[5]), .pin14(n7402_2_pin8[5]), .pin13(n7402_2_pin8[4]),
    .pin12(n74273_3_pin2[4]), .pin11(CLK));
  IC74245 ic74245_12 (
    .DIR(1'b0), .iOE(n7414_1_pin8), .B0(undriven_4[0]), .B1(undriven_4[1]), .B2(undriven_4[2]),
    .B3(undriven_4[3]), .B4(undriven_4[4]), .B5(undriven_4[5]), .B6(undriven_4[6]), .B7(undriven_4[7]),
    .A0(ic74245_12_a0[0]), .A1(ic74245_12_a0[1]), .A2(ic74245_12_a0[2]), .A3(ic74245_12_a0[3]),
    .A4(ic74245_12_a0[4]), .A5(ic74245_12_a0[5]), .A6(ic74245_12_a0[6]), .A7(ic74245_12_a0[7]));
  _7486 u_7486_3 (
    .pin1(ic74245_12_a0[4]), .pin2(n7414_2_pin6), .pin3(n74283_3_pin6), .pin4(ic74245_12_a0[5]),
    .pin5(n7414_2_pin6), .pin6(n74283_3_pin2), .pin13(n7414_2_pin6), .pin12(ic74245_12_a0[7]),
    .pin11(n74283_3_pin11), .pin10(n7414_2_pin6), .pin9(ic74245_12_a0[6]), .pin8(n74283_3_pin15));
  _74283 u_74283_4 (
    .pin1(n7402_2_pin8[1]), .pin2(n74283_4_pin2), .pin3(ic74245_9_a0[1]), .pin4(n7402_2_pin8[0]),
    .pin5(ic74245_9_a0[0]), .pin6(n74283_4_pin6), .pin7(n7414_2_pin6), .pin15(n74283_4_pin15),
    .pin14(ic74245_9_a0[2]), .pin13(n7402_2_pin8[2]), .pin12(ic74245_9_a0[3]), .pin11(n74283_4_pin11),
    .pin10(n7402_2_pin8[3]), .pin9(n74283_3_pin7));
  IC74245 ic74245_13 (
    .DIR(1'b0), .iOE(n7414_1_pin10), .B0(BLI[0]), .B1(BLI[1]), .B2(BLI[2]), .B3(BLI[3]), .B4(BLI[4]),
    .B5(BLI[5]), .B6(BLI[6]), .B7(BLI[7]), .A0(ic74245_12_a0[0]), .A1(ic74245_12_a0[1]),
    .A2(ic74245_12_a0[2]), .A3(ic74245_12_a0[3]), .A4(ic74245_12_a0[4]), .A5(ic74245_12_a0[5]),
    .A6(ic74245_12_a0[6]), .A7(ic74245_12_a0[7]));
  LedBar ledbar_5 (
    .led0(ic74245_14_a0[7]), .led1(ic74245_14_a0[6]), .led2(ic74245_14_a0[5]), .led3(ic74245_14_a0[4]),
    .led4(ic74245_14_a0[3]), .led5(ic74245_14_a0[2]), .led6(ic74245_14_a0[1]), .led7(ic74245_14_a0[0]));
  _7486 u_7486_4 (
    .pin1(ic74245_12_a0[0]), .pin2(n7414_2_pin6), .pin3(n74283_4_pin6), .pin4(ic74245_12_a0[1]),
    .pin5(n7414_2_pin6), .pin6(n74283_4_pin2), .pin13(n7414_2_pin6), .pin12(ic74245_12_a0[3]),
    .pin11(n74283_4_pin11), .pin10(n7414_2_pin6), .pin9(ic74245_12_a0[2]), .pin8(n74283_4_pin15));
  LedBar ledbar_6 (
    .led0(ic74245_15_a0[7]), .led1(ic74245_15_a0[6]), .led2(ic74245_15_a0[5]), .led3(ic74245_15_a0[4]),
    .led4(ic74245_15_a0[3]), .led5(ic74245_15_a0[2]), .led6(ic74245_15_a0[1]), .led7(ic74245_15_a0[0]));
  IC74245 ic74245_14 (
    .DIR(1'b0), .iOE(1'b0), .B0(ic74245_12_a0[0]), .B1(ic74245_12_a0[1]), .B2(ic74245_12_a0[2]),
    .B3(ic74245_12_a0[3]), .B4(ic74245_12_a0[4]), .B5(ic74245_12_a0[5]), .B6(ic74245_12_a0[6]),
    .B7(ic74245_12_a0[7]), .A0(ic74245_14_a0[0]), .A1(ic74245_14_a0[1]), .A2(ic74245_14_a0[2]),
    .A3(ic74245_14_a0[3]), .A4(ic74245_14_a0[4]), .A5(ic74245_14_a0[5]), .A6(ic74245_14_a0[6]),
    .A7(ic74245_14_a0[7]));
  IC74245 ic74245_15 (
    .DIR(1'b0), .iOE(1'b0), .B0(n74273_3_pin2[0]), .B1(n74273_3_pin2[1]), .B2(n74273_3_pin2[2]),
    .B3(n74273_3_pin2[3]), .B4(n74273_3_pin2[4]), .B5(n74273_3_pin2[5]), .B6(n74273_3_pin2[6]),
    .B7(n74273_3_pin2[7]), .A0(ic74245_15_a0[0]), .A1(ic74245_15_a0[1]), .A2(ic74245_15_a0[2]),
    .A3(ic74245_15_a0[3]), .A4(ic74245_15_a0[4]), .A5(ic74245_15_a0[5]), .A6(ic74245_15_a0[6]),
    .A7(ic74245_15_a0[7]));
  IC74245 ic74245_16 (
    .DIR(1'b0), .iOE(n7400_1_pin8), .B0(n74273_3_pin2[0]), .B1(n74273_3_pin2[1]), .B2(n74273_3_pin2[2]),
    .B3(n74273_3_pin2[3]), .B4(n74273_3_pin2[4]), .B5(n74273_3_pin2[5]), .B6(n74273_3_pin2[6]),
    .B7(n74273_3_pin2[7]), .A0(IBLO[0]), .A1(IBLO[1]), .A2(IBLO[2]), .A3(IBLO[3]), .A4(IBLO[4]),
    .A5(IBLO[5]), .A6(IBLO[6]), .A7(IBLO[7]));
  // also tied to GND on the sheet: {n7408_1_pin1, n7408_1_pin2, n74273_2_pin18, n74273_2_pin17, n7408_2_pin4, n7408_2_pin5}

  // Notes on the sheet:
  //   IBHO: pull=up
  //   BHI: pull=up
  //   Standalone: pull=up
  //   nRST: pull=up
  //   SFW: pull=up
  //   SNH: pull=up
  //   RHOE: pull=up
  //   SFL: pull=up
  //   CFL: pull=up
  //   ZFL: pull=up
  //   SFH: pull=up
  //   RLOE: pull=up
  //   CFH: pull=up
  //   ZFH: pull=up
  //   SNL: pull=up
  //   ALI: pull=up
  //   BLI: pull=up
  //   IBLO: pull=up
  //   AHI: pull=up
  //   AH
  //   RH
  //   BH
  //   FR
  //   AL
  //   RL
  //   BL
endmodule
