// Logisim project TalosES_CTRL_gates.circ as structural Verilog: 1 circuit, main circuit main
module main (
  input  SIMF,
  input  COMF,
  output PCOE,
  output CLK
);

  wire and_1_out, and_2_out, and_3_out, and_7_out, and_8_out, CIMF, d_ff_2_q, d_ff_2_qn, d_ff_3_q, d_ff_3_qn,
       d_ff_4_qn, IMF, nCLK, nHLT, nOE, not_1_out, not_2_out, not_3_out, nRST, nSYSCLK, OMF, or_1_out,
       or_2_out, plarom_1_p1, plarom_1_p4, SOMF, SYSCLK;

  // PlaRom #(.Contents("2 1*8 2 1*6 2 2 1*8 2 1*5 2 1 2 1*6 2 2 1*5 0*6"), .\and (6), .outputs(1)) plarom_1: pin names not known; wires that end beside it: plarom_1_p1, plarom_1_p1, 1'b0, plarom_1_p4
  not not_1 (not_1_out, SOMF);
  D_Flip_Flop d_ff_1 (.D(1'b0), .clk(1'b0), .Q(OMF), .preset(not_1_out), .reset(or_1_out));  // open: Qn
  or or_1 (or_1_out, nRST, COMF);
  D_Flip_Flop d_ff_2 (.D(nHLT), .clk(SYSCLK), .Q(d_ff_2_q), .Qn(d_ff_2_qn), .reset(nRST));  // open: preset
  D_Flip_Flop d_ff_3 (.D(and_1_out), .clk(nCLK), .Q(d_ff_3_q), .Qn(d_ff_3_qn), .reset(nRST));  // open: preset
  and and_1 (and_1_out, plarom_1_p4, d_ff_3_qn);
  and and_2 (and_2_out, nRST, nRST);
  D_Flip_Flop d_ff_4 (.D(d_ff_2_qn), .clk(nSYSCLK), .Q(nOE), .Qn(d_ff_4_qn), .preset(nRST));  // open: reset
  not not_2 (not_2_out, SIMF);
  D_Flip_Flop d_ff_5 (.D(1'b0), .clk(1'b0), .Q(IMF), .preset(not_2_out), .reset(or_2_out));  // open: Qn
  or or_2 (or_2_out, nRST, not_3_out);
  not not_3 (not_3_out, CIMF);
  and and_3 (and_3_out, d_ff_3_q, d_ff_3_q);
  and and_4 (PCOE, and_2_out, and_2_out);
  and and_5 (nCLK, nSYSCLK, d_ff_2_q);
  and and_6 (CLK, d_ff_4_qn, SYSCLK);
  and and_7 (and_7_out, and_3_out, and_3_out);
  and and_8 (and_8_out, and_7_out, and_7_out);

  // Notes on the sheet:
  //   COMF: pull=up
  //   SIMF: pull=up
  //   opcode/imm
  //   A little delay
  //   SYSCLK
  //   nOE of NOP generator
  //   Halt
  //   Disable CLK
  //   Disable nCLK
  //   Disable transceivers
endmodule
