// Logisim project DEMUX.circ as structural Verilog: 1 circuit, main circuit main
module main (
  input  SLC0,
  input  SLC1,
  input  SLC2
);

  wire n74138_1_pin4, n74138_1_pin5, n74138_1_pin6, n74138_1_pin7, n74138_1_pin9, n74138_1_pin10,
       n74138_1_pin11, n74138_1_pin12, n74138_1_pin13, n74138_1_pin14, n74138_1_pin15;

  _74138 u_74138_1 (
    .pin1(SLC0), .pin2(SLC1), .pin3(SLC2), .pin4(n74138_1_pin4), .pin5(n74138_1_pin5), .pin6(n74138_1_pin6),
    .pin7(n74138_1_pin7), .pin15(n74138_1_pin15), .pin14(n74138_1_pin14), .pin13(n74138_1_pin13),
    .pin12(n74138_1_pin12), .pin11(n74138_1_pin11), .pin10(n74138_1_pin10), .pin9(n74138_1_pin9));
  LED led_1 (.in(n74138_1_pin15));
  LED led_2 (.in(n74138_1_pin14));
  LED led_3 (.in(n74138_1_pin13));
  LED led_4 (.in(n74138_1_pin12));
  LED led_5 (.in(n74138_1_pin11));
  LED led_6 (.in(n74138_1_pin10));
  LED led_7 (.in(n74138_1_pin9));
  LED led_8 (.in(n74138_1_pin7));
  // also tied to GND on the sheet: {n74138_1_pin4, n74138_1_pin5}
  // also tied to VCC on the sheet: n74138_1_pin6
endmodule
