// Logisim project clockDivider.circ as structural Verilog: 1 circuit, main circuit main
module main (
  input  CLR1,
  input  nRST1,
  input  CLK1,
  input  CLR2,
  input  nRST2,
  input  CLK2
);

  wire d_ff_1_q, d_ff_1_qn, n74161_1_pin3, n74161_1_pin4, n74161_1_pin5, n74161_1_pin6, n74161_1_pin7,
       n74161_1_pin9, n74161_1_pin10, n74161_1_pin11, n74161_1_pin12, n74161_1_pin13, n74161_1_pin14,
       n74161_1_pin15, n74161_2_pin3, n74161_2_pin4, n74161_2_pin5, n74161_2_pin6, n74161_2_pin7,
       n74161_2_pin9, n74161_2_pin10, n74161_2_pin11, n74161_2_pin12, n74161_2_pin13, n74161_2_pin14,
       n74161_2_pin15;

  LED led_1 (.in(n74161_1_pin15));
  LED led_2 (.in(n74161_1_pin14));
  _74161 u_74161_1 (
    .pin1(nRST1), .pin2(CLK1), .pin3(n74161_1_pin3), .pin4(n74161_1_pin4), .pin5(n74161_1_pin5),
    .pin6(n74161_1_pin6), .pin7(n74161_1_pin7), .pin15(n74161_1_pin15), .pin14(n74161_1_pin14),
    .pin13(n74161_1_pin13), .pin12(n74161_1_pin12), .pin11(n74161_1_pin11), .pin10(n74161_1_pin10),
    .pin9(n74161_1_pin9));
  DipSwitch #(.number(4)) dipswitch_1 (
    .sw1(n74161_1_pin3), .sw2(n74161_1_pin4), .sw3(n74161_1_pin5), .sw4(n74161_1_pin6));
  LED led_3 (.in(n74161_2_pin15));
  LED led_4 (.in(n74161_2_pin14));
  _74161 u_74161_2 (
    .pin1(nRST2), .pin2(CLK2), .pin3(n74161_2_pin3), .pin4(n74161_2_pin4), .pin5(n74161_2_pin5),
    .pin6(n74161_2_pin6), .pin7(n74161_2_pin7), .pin15(n74161_2_pin15), .pin14(n74161_2_pin14),
    .pin13(n74161_2_pin13), .pin12(n74161_2_pin12), .pin11(n74161_2_pin11), .pin10(n74161_2_pin10),
    .pin9(n74161_2_pin9));
  DipSwitch #(.number(4)) dipswitch_2 (
    .sw1(n74161_2_pin3), .sw2(n74161_2_pin4), .sw3(n74161_2_pin5), .sw4(n74161_2_pin6));
  not not_1 (n74161_1_pin9, n74161_1_pin15);
  LED led_5 (.in(n74161_1_pin13));
  LED led_6 (.in(n74161_1_pin12));
  LED led_7 (.in(n74161_1_pin11));
  not not_2 (n74161_2_pin9, n74161_2_pin15);
  LED led_8 (.in(n74161_2_pin13));
  LED led_9 (.in(n74161_2_pin12));
  LED led_10 (.in(n74161_2_pin11));
  D_Flip_Flop d_ff_1 (.D(d_ff_1_qn), .clk(n74161_2_pin9), .Q(d_ff_1_q), .Qn(d_ff_1_qn), .preset(1'b0), .reset(1'b0));
  // Digital_Oscilloscope #(.nState(25)) digital_oscilloscope_1: pin names not known; wires that end beside it: CLK1, n74161_1_pin9, CLR1
  // Digital_Oscilloscope #(.nState(25)) digital_oscilloscope_2: pin names not known; wires that end beside it: CLK2, d_ff_1_q, n74161_2_pin9, CLR2
  // also tied to VCC on the sheet: {n74161_1_pin10, n74161_1_pin7, n74161_2_pin10, n74161_2_pin7}
endmodule
