// Logisim project TalosEF_RF_card.circ as structural Verilog: 1 circuit, main circuit RF
module RF (
  input  [7:0] IBHI,
  input  [7:0] IBLI,
  input  BHLE,
  input  BLLE,
  input  AHLE,
  input  ALLE,
  input  EDBIEH,
  input  EDBIEL,
  input  IBHOE,
  input  IBLOE,
  input  BHOE,
  input  BLOE,
  input  AHOE,
  input  ALOE,
  input  [7:0] EDBI,
  output [7:0] AHO,
  output [7:0] BHO,
  output [7:0] ALO,
  output [7:0] BLO,
  output [7:0] IBHO,
  output [7:0] IBLO,
  output [7:0] EDBO
);

  wire CLK, n7414_1_pin2, n7414_1_pin4, n7414_1_pin6, n7414_1_pin8, n7414_1_pin10, n7414_1_pin12,
       n7414_2_pin2, n7414_2_pin4, n7414_2_pin6, n7414_2_pin8, n7414_2_pin10, n7414_2_pin12;
  wire [7:0] ic74245_1_a0, ic74245_6_a0;

  _7414 u_7414_1 (
    .pin1(IBHOE), .pin2(n7414_1_pin2), .pin3(BHOE), .pin4(n7414_1_pin4), .pin5(AHOE), .pin6(n7414_1_pin6),
    .pin13(EDBIEH), .pin12(n7414_1_pin12), .pin11(AHLE), .pin10(n7414_1_pin10), .pin9(BHLE),
    .pin8(n7414_1_pin8));
  _74377 u_74377_1 (
    .pin1(n7414_1_pin10), .pin2(AHO[0]), .pin3(IBHI[0]), .pin4(IBHI[1]), .pin5(AHO[1]), .pin6(AHO[2]),
    .pin7(IBHI[2]), .pin8(IBHI[3]), .pin9(AHO[3]), .pin19(AHO[7]), .pin18(IBHI[7]), .pin17(IBHI[6]),
    .pin16(AHO[6]), .pin15(AHO[5]), .pin14(IBHI[5]), .pin13(IBHI[4]), .pin12(AHO[4]), .pin11(CLK));
  IC74245 ic74245_1 (
    .DIR(1'b0), .iOE(n7414_1_pin6), .B0(AHO[0]), .B1(AHO[1]), .B2(AHO[2]), .B3(AHO[3]), .B4(AHO[4]),
    .B5(AHO[5]), .B6(AHO[6]), .B7(AHO[7]), .A0(ic74245_1_a0[0]), .A1(ic74245_1_a0[1]), .A2(ic74245_1_a0[2]),
    .A3(ic74245_1_a0[3]), .A4(ic74245_1_a0[4]), .A5(ic74245_1_a0[5]), .A6(ic74245_1_a0[6]),
    .A7(ic74245_1_a0[7]));
  IC74245 ic74245_2 (
    .DIR(1'b0), .iOE(n7414_1_pin12), .B0(EDBI[0]), .B1(EDBI[1]), .B2(EDBI[2]), .B3(EDBI[3]), .B4(EDBI[4]),
    .B5(EDBI[5]), .B6(EDBI[6]), .B7(EDBI[7]), .A0(ic74245_1_a0[0]), .A1(ic74245_1_a0[1]),
    .A2(ic74245_1_a0[2]), .A3(ic74245_1_a0[3]), .A4(ic74245_1_a0[4]), .A5(ic74245_1_a0[5]),
    .A6(ic74245_1_a0[6]), .A7(ic74245_1_a0[7]));
  _74377 u_74377_2 (
    .pin1(n7414_1_pin8), .pin2(BHO[0]), .pin3(IBHI[0]), .pin4(IBHI[1]), .pin5(BHO[1]), .pin6(BHO[2]),
    .pin7(IBHI[2]), .pin8(IBHI[3]), .pin9(BHO[3]), .pin19(BHO[7]), .pin18(IBHI[7]), .pin17(IBHI[6]),
    .pin16(BHO[6]), .pin15(BHO[5]), .pin14(IBHI[5]), .pin13(IBHI[4]), .pin12(BHO[4]), .pin11(CLK));
  IC74245 ic74245_3 (
    .DIR(1'b0), .iOE(n7414_1_pin4), .B0(BHO[0]), .B1(BHO[1]), .B2(BHO[2]), .B3(BHO[3]), .B4(BHO[4]),
    .B5(BHO[5]), .B6(BHO[6]), .B7(BHO[7]), .A0(IBHO[0]), .A1(IBHO[1]), .A2(IBHO[2]), .A3(IBHO[3]),
    .A4(IBHO[4]), .A5(IBHO[5]), .A6(IBHO[6]), .A7(IBHO[7]));
  IC74245 ic74245_4 (
    .DIR(1'b0), .iOE(n7414_1_pin2), .B0(IBHI[0]), .B1(IBHI[1]), .B2(IBHI[2]), .B3(IBHI[3]), .B4(IBHI[4]),
    .B5(IBHI[5]), .B6(IBHI[6]), .B7(IBHI[7]), .A0(EDBO[0]), .A1(EDBO[1]), .A2(EDBO[2]), .A3(EDBO[3]),
    .A4(EDBO[4]), .A5(EDBO[5]), .A6(EDBO[6]), .A7(EDBO[7]));
  _7414 u_7414_2 (
    .pin1(IBLOE), .pin2(n7414_2_pin2), .pin3(BLOE), .pin4(n7414_2_pin4), .pin5(ALOE), .pin6(n7414_2_pin6),
    .pin13(EDBIEL), .pin12(n7414_2_pin12), .pin11(ALLE), .pin10(n7414_2_pin10), .pin9(BLLE),
    .pin8(n7414_2_pin8));
  IC74245 ic74245_5 (
    .DIR(1'b0), .iOE(n7414_2_pin2), .B0(IBLI[0]), .B1(IBLI[1]), .B2(IBLI[2]), .B3(IBLI[3]), .B4(IBLI[4]),
    .B5(IBLI[5]), .B6(IBLI[6]), .B7(IBLI[7]), .A0(EDBO[0]), .A1(EDBO[1]), .A2(EDBO[2]), .A3(EDBO[3]),
    .A4(EDBO[4]), .A5(EDBO[5]), .A6(EDBO[6]), .A7(EDBO[7]));
  _74377 u_74377_3 (
    .pin1(n7414_2_pin10), .pin2(ALO[0]), .pin3(IBLI[0]), .pin4(IBLI[1]), .pin5(ALO[1]), .pin6(ALO[2]),
    .pin7(IBLI[2]), .pin8(IBLI[3]), .pin9(ALO[3]), .pin19(ALO[7]), .pin18(IBLI[7]), .pin17(IBLI[6]),
    .pin16(ALO[6]), .pin15(ALO[5]), .pin14(IBLI[5]), .pin13(IBLI[4]), .pin12(ALO[4]), .pin11(CLK));
  IC74245 ic74245_6 (
    .DIR(1'b0), .iOE(n7414_2_pin6), .B0(ALO[0]), .B1(ALO[1]), .B2(ALO[2]), .B3(ALO[3]), .B4(ALO[4]),
    .B5(ALO[5]), .B6(ALO[6]), .B7(ALO[7]), .A0(ic74245_6_a0[0]), .A1(ic74245_6_a0[1]), .A2(ic74245_6_a0[2]),
    .A3(ic74245_6_a0[3]), .A4(ic74245_6_a0[4]), .A5(ic74245_6_a0[5]), .A6(ic74245_6_a0[6]),
    .A7(ic74245_6_a0[7]));
  IC74245 ic74245_7 (
    .DIR(1'b0), .iOE(n7414_2_pin12), .B0(EDBI[0]), .B1(EDBI[1]), .B2(EDBI[2]), .B3(EDBI[3]), .B4(EDBI[4]),
    .B5(EDBI[5]), .B6(EDBI[6]), .B7(EDBI[7]), .A0(ic74245_6_a0[0]), .A1(ic74245_6_a0[1]),
    .A2(ic74245_6_a0[2]), .A3(ic74245_6_a0[3]), .A4(ic74245_6_a0[4]), .A5(ic74245_6_a0[5]),
    .A6(ic74245_6_a0[6]), .A7(ic74245_6_a0[7]));
  _74377 u_74377_4 (
    .pin1(n7414_2_pin8), .pin2(BLO[0]), .pin3(IBLI[0]), .pin4(IBLI[1]), .pin5(BLO[1]), .pin6(BLO[2]),
    .pin7(IBLI[2]), .pin8(IBLI[3]), .pin9(BLO[3]), .pin19(BLO[7]), .pin18(IBLI[7]), .pin17(IBLI[6]),
    .pin16(BLO[6]), .pin15(BLO[5]), .pin14(IBLI[5]), .pin13(IBLI[4]), .pin12(BLO[4]), .pin11(CLK));
  IC74245 ic74245_8 (
    .DIR(1'b0), .iOE(n7414_2_pin4), .B0(BLO[0]), .B1(BLO[1]), .B2(BLO[2]), .B3(BLO[3]), .B4(BLO[4]),
    .B5(BLO[5]), .B6(BLO[6]), .B7(BLO[7]), .A0(IBLO[0]), .A1(IBLO[1]), .A2(IBLO[2]), .A3(IBLO[3]),
    .A4(IBLO[4]), .A5(IBLO[5]), .A6(IBLO[6]), .A7(IBLO[7]));

  // Notes on the sheet:
  //   BHO: pull=up
  //   BHLE: pull=up
  //   AHLE: pull=up
  //   EDBIEH: pull=up
  //   IBHOE: pull=up
  //   BHOE: pull=up
  //   AHOE: pull=up
  //   EDBO: pull=up
  //   BLLE: pull=up
  //   ALLE: pull=up
  //   EDBIEL: pull=up
  //   IBLOE: pull=up
  //   BLOE: pull=up
  //   ALOE: pull=up
  //   ALO: pull=up
  //   IBLO: pull=up
  //   BLO: pull=up
  //   AHO: pull=up
  //   IBHO: pull=up
  //   AH
  //   BH
  //   AL
  //   BL
endmodule
