// Logisim project TalosES_RF_testbed.circ as structural Verilog: 1 circuit, main circuit RF
module RF (
  input  [7:0] IBL,
  input  [7:0] IBH,
  input  CLK,
  input  Standalone,
  input  BHLE,
  input  BLLE,
  input  AHLE,
  input  ALLE,
  input  IBHIOE,
  input  IBLIOE,
  input  BHOE,
  input  BLOE,
  input  AHOE,
  input  ALOE,
  input  EDBIE,
  output [7:0] AHO,
  output [7:0] BHO,
  output [7:0] ALO,
  output [7:0] BLO,
  output [7:0] EDB
);

  wire n7408_1_pin1, n7408_1_pin2, n7408_1_pin3, n7408_1_pin4, n7408_1_pin5, n7408_1_pin6, n7414_1_pin2,
       n7414_1_pin4, n7414_1_pin6, n7414_1_pin8, n7414_1_pin10, n7414_2_pin2, n7414_2_pin4, n7414_2_pin6,
       n7414_2_pin8, n7414_2_pin10, n7414_2_pin12, n7414_2_pin13, n7432_1_pin3, n7432_1_pin5, n7432_1_pin6,
       n7432_1_pin8, n7432_1_pin11, n7432_1_pin12, n7432_1_pin13, n7432_2_pin3, n7432_2_pin5, n7432_2_pin6,
       n7432_2_pin8, n7432_2_pin11, n7432_2_pin12, n7432_2_pin13, n74377_1_pin2, n74377_1_pin5,
       n74377_1_pin6, n74377_1_pin9, n74377_1_pin12, n74377_1_pin15, n74377_1_pin16, n74377_1_pin19,
       n74377_2_pin2, n74377_2_pin5, n74377_2_pin6, n74377_2_pin9, n74377_2_pin12, n74377_2_pin15,
       n74377_2_pin16, n74377_2_pin19, n74377_3_pin2, n74377_3_pin5, n74377_3_pin6, n74377_3_pin9,
       n74377_3_pin12, n74377_3_pin15, n74377_3_pin16, n74377_3_pin19, n74377_4_pin2, n74377_4_pin5,
       n74377_4_pin6, n74377_4_pin9, n74377_4_pin12, n74377_4_pin15, n74377_4_pin16, n74377_4_pin19,
       NOTstandalone;
  wire [7:0] dipswitch_1_sw8, dipswitch_2_sw8, ic74245_3_a0, ic74245_4_a0, ic74245_7_a0, ic74245_11_a0,
       ic74245_14_a0, ic74245_17_a0, ic74245_20_a0, n74377_1_pin3;

  _7414 u_7414_1 (
    .pin1(IBHIOE), .pin2(n7414_1_pin2), .pin3(BHOE), .pin4(n7414_1_pin4), .pin5(AHOE), .pin6(n7414_1_pin6),
    .pin13(Standalone), .pin12(NOTstandalone), .pin11(AHLE), .pin10(n7414_1_pin10), .pin9(BHLE),
    .pin8(n7414_1_pin8));
  _74377 u_74377_1 (
    .pin1(n7414_1_pin10), .pin2(n74377_1_pin2), .pin3(n74377_1_pin3[0]), .pin4(n74377_1_pin3[1]),
    .pin5(n74377_1_pin5), .pin6(n74377_1_pin6), .pin7(n74377_1_pin3[2]), .pin8(n74377_1_pin3[3]),
    .pin9(n74377_1_pin9), .pin19(n74377_1_pin19), .pin18(n74377_1_pin3[7]), .pin17(n74377_1_pin3[6]),
    .pin16(n74377_1_pin16), .pin15(n74377_1_pin15), .pin14(n74377_1_pin3[5]), .pin13(n74377_1_pin3[4]),
    .pin12(n74377_1_pin12), .pin11(CLK));
  _7432 u_7432_1 (
    .pin1(AHOE), .pin2(BHOE), .pin3(n7432_1_pin3), .pin4(n7432_1_pin3), .pin5(n7432_1_pin5),
    .pin6(n7432_1_pin6), .pin13(n7432_1_pin13), .pin12(n7432_1_pin12), .pin11(n7432_1_pin11),
    .pin10(NOTstandalone), .pin9(n7432_1_pin6), .pin8(n7432_1_pin8));
  _7432 u_7432_2 (
    .pin1(ALOE), .pin2(BLOE), .pin3(n7432_2_pin3), .pin4(n7432_2_pin3), .pin5(n7432_2_pin5),
    .pin6(n7432_2_pin6), .pin13(n7432_2_pin13), .pin12(n7432_2_pin12), .pin11(n7432_2_pin11),
    .pin10(NOTstandalone), .pin9(n7432_2_pin6), .pin8(n7432_2_pin8));
  IC74245 ic74245_1 (
    .DIR(1'b0), .iOE(1'b0), .B0(n74377_1_pin2), .B1(n74377_1_pin5), .B2(n74377_1_pin6), .B3(n74377_1_pin9),
    .B4(n74377_1_pin12), .B5(n74377_1_pin15), .B6(n74377_1_pin16), .B7(n74377_1_pin19), .A0(AHO[0]),
    .A1(AHO[1]), .A2(AHO[2]), .A3(AHO[3]), .A4(AHO[4]), .A5(AHO[5]), .A6(AHO[6]), .A7(AHO[7]));
  // NoConnect on n7432_1_pin11
  // NoConnect on n7432_2_pin11
  LedBar ledbar_1 (
    .led0(ic74245_3_a0[7]), .led1(ic74245_3_a0[6]), .led2(ic74245_3_a0[5]), .led3(ic74245_3_a0[4]),
    .led4(ic74245_3_a0[3]), .led5(ic74245_3_a0[2]), .led6(ic74245_3_a0[1]), .led7(ic74245_3_a0[0]));
  IC74245 ic74245_2 (
    .DIR(1'b0), .iOE(n7414_1_pin6), .B0(n74377_1_pin2), .B1(n74377_1_pin5), .B2(n74377_1_pin6),
    .B3(n74377_1_pin9), .B4(n74377_1_pin12), .B5(n74377_1_pin15), .B6(n74377_1_pin16), .B7(n74377_1_pin19),
    .A0(n74377_1_pin3[0]), .A1(n74377_1_pin3[1]), .A2(n74377_1_pin3[2]), .A3(n74377_1_pin3[3]),
    .A4(n74377_1_pin3[4]), .A5(n74377_1_pin3[5]), .A6(n74377_1_pin3[6]), .A7(n74377_1_pin3[7]));
  IC74245 ic74245_3 (
    .DIR(1'b0), .iOE(1'b0), .B0(n74377_1_pin2), .B1(n74377_1_pin5), .B2(n74377_1_pin6), .B3(n74377_1_pin9),
    .B4(n74377_1_pin12), .B5(n74377_1_pin15), .B6(n74377_1_pin16), .B7(n74377_1_pin19), .A0(ic74245_3_a0[0]),
    .A1(ic74245_3_a0[1]), .A2(ic74245_3_a0[2]), .A3(ic74245_3_a0[3]), .A4(ic74245_3_a0[4]),
    .A5(ic74245_3_a0[5]), .A6(ic74245_3_a0[6]), .A7(ic74245_3_a0[7]));
  _7408 u_7408_1 (
    .pin1(n7408_1_pin1), .pin2(n7408_1_pin2), .pin3(n7408_1_pin3), .pin4(n7408_1_pin4), .pin5(n7408_1_pin5),
    .pin6(n7408_1_pin6), .pin13(EDBIE), .pin12(IBHIOE), .pin11(n7432_1_pin5), .pin10(EDBIE), .pin9(IBLIOE),
    .pin8(n7432_2_pin5));
  // NoConnect on n7408_1_pin3
  // NoConnect on n7408_1_pin6
  _74377 u_74377_2 (
    .pin1(n7414_1_pin8), .pin2(n74377_2_pin2), .pin3(n74377_1_pin3[0]), .pin4(n74377_1_pin3[1]),
    .pin5(n74377_2_pin5), .pin6(n74377_2_pin6), .pin7(n74377_1_pin3[2]), .pin8(n74377_1_pin3[3]),
    .pin9(n74377_2_pin9), .pin19(n74377_2_pin19), .pin18(n74377_1_pin3[7]), .pin17(n74377_1_pin3[6]),
    .pin16(n74377_2_pin16), .pin15(n74377_2_pin15), .pin14(n74377_1_pin3[5]), .pin13(n74377_1_pin3[4]),
    .pin12(n74377_2_pin12), .pin11(CLK));
  DipSwitch dipswitch_1 (
    .sw1(dipswitch_1_sw8[7]), .sw2(dipswitch_1_sw8[6]), .sw3(dipswitch_1_sw8[5]), .sw4(dipswitch_1_sw8[4]),
    .sw5(dipswitch_1_sw8[3]), .sw6(dipswitch_1_sw8[2]), .sw7(dipswitch_1_sw8[1]), .sw8(dipswitch_1_sw8[0]));
  LedBar ledbar_2 (
    .led0(ic74245_4_a0[7]), .led1(ic74245_4_a0[6]), .led2(ic74245_4_a0[5]), .led3(ic74245_4_a0[4]),
    .led4(ic74245_4_a0[3]), .led5(ic74245_4_a0[2]), .led6(ic74245_4_a0[1]), .led7(ic74245_4_a0[0]));
  IC74245 ic74245_4 (
    .DIR(1'b0), .iOE(1'b0), .B0(n74377_1_pin3[0]), .B1(n74377_1_pin3[1]), .B2(n74377_1_pin3[2]),
    .B3(n74377_1_pin3[3]), .B4(n74377_1_pin3[4]), .B5(n74377_1_pin3[5]), .B6(n74377_1_pin3[6]),
    .B7(n74377_1_pin3[7]), .A0(ic74245_4_a0[0]), .A1(ic74245_4_a0[1]), .A2(ic74245_4_a0[2]),
    .A3(ic74245_4_a0[3]), .A4(ic74245_4_a0[4]), .A5(ic74245_4_a0[5]), .A6(ic74245_4_a0[6]),
    .A7(ic74245_4_a0[7]));
  IC74245 ic74245_5 (
    .DIR(1'b0), .iOE(1'b0), .B0(n74377_2_pin2), .B1(n74377_2_pin5), .B2(n74377_2_pin6), .B3(n74377_2_pin9),
    .B4(n74377_2_pin12), .B5(n74377_2_pin15), .B6(n74377_2_pin16), .B7(n74377_2_pin19), .A0(BHO[0]),
    .A1(BHO[1]), .A2(BHO[2]), .A3(BHO[3]), .A4(BHO[4]), .A5(BHO[5]), .A6(BHO[6]), .A7(BHO[7]));
  LedBar ledbar_3 (
    .led0(ic74245_7_a0[7]), .led1(ic74245_7_a0[6]), .led2(ic74245_7_a0[5]), .led3(ic74245_7_a0[4]),
    .led4(ic74245_7_a0[3]), .led5(ic74245_7_a0[2]), .led6(ic74245_7_a0[1]), .led7(ic74245_7_a0[0]));
  IC74245 ic74245_6 (
    .DIR(1'b0), .iOE(n7414_1_pin4), .B0(n74377_2_pin2), .B1(n74377_2_pin5), .B2(n74377_2_pin6),
    .B3(n74377_2_pin9), .B4(n74377_2_pin12), .B5(n74377_2_pin15), .B6(n74377_2_pin16), .B7(n74377_2_pin19),
    .A0(n74377_1_pin3[0]), .A1(n74377_1_pin3[1]), .A2(n74377_1_pin3[2]), .A3(n74377_1_pin3[3]),
    .A4(n74377_1_pin3[4]), .A5(n74377_1_pin3[5]), .A6(n74377_1_pin3[6]), .A7(n74377_1_pin3[7]));
  IC74245 ic74245_7 (
    .DIR(1'b0), .iOE(1'b0), .B0(n74377_2_pin2), .B1(n74377_2_pin5), .B2(n74377_2_pin6), .B3(n74377_2_pin9),
    .B4(n74377_2_pin12), .B5(n74377_2_pin15), .B6(n74377_2_pin16), .B7(n74377_2_pin19), .A0(ic74245_7_a0[0]),
    .A1(ic74245_7_a0[1]), .A2(ic74245_7_a0[2]), .A3(ic74245_7_a0[3]), .A4(ic74245_7_a0[4]),
    .A5(ic74245_7_a0[5]), .A6(ic74245_7_a0[6]), .A7(ic74245_7_a0[7]));
  IC74245 ic74245_8 (
    .DIR(n7432_1_pin6), .iOE(Standalone), .B0(IBH[0]), .B1(IBH[1]), .B2(IBH[2]), .B3(IBH[3]), .B4(IBH[4]),
    .B5(IBH[5]), .B6(IBH[6]), .B7(IBH[7]), .A0(n74377_1_pin3[0]), .A1(n74377_1_pin3[1]),
    .A2(n74377_1_pin3[2]), .A3(n74377_1_pin3[3]), .A4(n74377_1_pin3[4]), .A5(n74377_1_pin3[5]),
    .A6(n74377_1_pin3[6]), .A7(n74377_1_pin3[7]));
  IC74245 ic74245_9 (
    .DIR(1'b0), .iOE(n7432_1_pin8), .B0(dipswitch_1_sw8[0]), .B1(dipswitch_1_sw8[1]),
    .B2(dipswitch_1_sw8[2]), .B3(dipswitch_1_sw8[3]), .B4(dipswitch_1_sw8[4]), .B5(dipswitch_1_sw8[5]),
    .B6(dipswitch_1_sw8[6]), .B7(dipswitch_1_sw8[7]), .A0(n74377_1_pin3[0]), .A1(n74377_1_pin3[1]),
    .A2(n74377_1_pin3[2]), .A3(n74377_1_pin3[3]), .A4(n74377_1_pin3[4]), .A5(n74377_1_pin3[5]),
    .A6(n74377_1_pin3[6]), .A7(n74377_1_pin3[7]));
  IC74245 ic74245_10 (
    .DIR(EDBIE), .iOE(n7414_1_pin2), .B0(n74377_1_pin3[0]), .B1(n74377_1_pin3[1]), .B2(n74377_1_pin3[2]),
    .B3(n74377_1_pin3[3]), .B4(n74377_1_pin3[4]), .B5(n74377_1_pin3[5]), .B6(n74377_1_pin3[6]),
    .B7(n74377_1_pin3[7]), .A0(EDB[0]), .A1(EDB[1]), .A2(EDB[2]), .A3(EDB[3]), .A4(EDB[4]), .A5(EDB[5]),
    .A6(EDB[6]), .A7(EDB[7]));
  IC74245 ic74245_11 (
    .DIR(n7432_2_pin6), .iOE(Standalone), .B0(IBL[0]), .B1(IBL[1]), .B2(IBL[2]), .B3(IBL[3]), .B4(IBL[4]),
    .B5(IBL[5]), .B6(IBL[6]), .B7(IBL[7]), .A0(ic74245_11_a0[0]), .A1(ic74245_11_a0[1]),
    .A2(ic74245_11_a0[2]), .A3(ic74245_11_a0[3]), .A4(ic74245_11_a0[4]), .A5(ic74245_11_a0[5]),
    .A6(ic74245_11_a0[6]), .A7(ic74245_11_a0[7]));
  IC74245 ic74245_12 (
    .DIR(1'b0), .iOE(n7432_2_pin8), .B0(dipswitch_2_sw8[0]), .B1(dipswitch_2_sw8[1]),
    .B2(dipswitch_2_sw8[2]), .B3(dipswitch_2_sw8[3]), .B4(dipswitch_2_sw8[4]), .B5(dipswitch_2_sw8[5]),
    .B6(dipswitch_2_sw8[6]), .B7(dipswitch_2_sw8[7]), .A0(ic74245_11_a0[0]), .A1(ic74245_11_a0[1]),
    .A2(ic74245_11_a0[2]), .A3(ic74245_11_a0[3]), .A4(ic74245_11_a0[4]), .A5(ic74245_11_a0[5]),
    .A6(ic74245_11_a0[6]), .A7(ic74245_11_a0[7]));
  _7414 u_7414_2 (
    .pin1(IBLIOE), .pin2(n7414_2_pin2), .pin3(BLOE), .pin4(n7414_2_pin4), .pin5(ALOE), .pin6(n7414_2_pin6),
    .pin13(n7414_2_pin13), .pin12(n7414_2_pin12), .pin11(ALLE), .pin10(n7414_2_pin10), .pin9(BLLE),
    .pin8(n7414_2_pin8));
  // NoConnect on n7414_2_pin12
  IC74245 ic74245_13 (
    .DIR(EDBIE), .iOE(n7414_2_pin2), .B0(ic74245_11_a0[0]), .B1(ic74245_11_a0[1]), .B2(ic74245_11_a0[2]),
    .B3(ic74245_11_a0[3]), .B4(ic74245_11_a0[4]), .B5(ic74245_11_a0[5]), .B6(ic74245_11_a0[6]),
    .B7(ic74245_11_a0[7]), .A0(EDB[0]), .A1(EDB[1]), .A2(EDB[2]), .A3(EDB[3]), .A4(EDB[4]), .A5(EDB[5]),
    .A6(EDB[6]), .A7(EDB[7]));
  IC74245 ic74245_14 (
    .DIR(1'b0), .iOE(1'b0), .B0(ic74245_11_a0[0]), .B1(ic74245_11_a0[1]), .B2(ic74245_11_a0[2]),
    .B3(ic74245_11_a0[3]), .B4(ic74245_11_a0[4]), .B5(ic74245_11_a0[5]), .B6(ic74245_11_a0[6]),
    .B7(ic74245_11_a0[7]), .A0(ic74245_14_a0[0]), .A1(ic74245_14_a0[1]), .A2(ic74245_14_a0[2]),
    .A3(ic74245_14_a0[3]), .A4(ic74245_14_a0[4]), .A5(ic74245_14_a0[5]), .A6(ic74245_14_a0[6]),
    .A7(ic74245_14_a0[7]));
  DipSwitch dipswitch_2 (
    .sw1(dipswitch_2_sw8[7]), .sw2(dipswitch_2_sw8[6]), .sw3(dipswitch_2_sw8[5]), .sw4(dipswitch_2_sw8[4]),
    .sw5(dipswitch_2_sw8[3]), .sw6(dipswitch_2_sw8[2]), .sw7(dipswitch_2_sw8[1]), .sw8(dipswitch_2_sw8[0]));
  LedBar ledbar_4 (
    .led0(ic74245_14_a0[7]), .led1(ic74245_14_a0[6]), .led2(ic74245_14_a0[5]), .led3(ic74245_14_a0[4]),
    .led4(ic74245_14_a0[3]), .led5(ic74245_14_a0[2]), .led6(ic74245_14_a0[1]), .led7(ic74245_14_a0[0]));
  _74377 u_74377_3 (
    .pin1(n7414_2_pin10), .pin2(n74377_3_pin2), .pin3(ic74245_11_a0[0]), .pin4(ic74245_11_a0[1]),
    .pin5(n74377_3_pin5), .pin6(n74377_3_pin6), .pin7(ic74245_11_a0[2]), .pin8(ic74245_11_a0[3]),
    .pin9(n74377_3_pin9), .pin19(n74377_3_pin19), .pin18(ic74245_11_a0[7]), .pin17(ic74245_11_a0[6]),
    .pin16(n74377_3_pin16), .pin15(n74377_3_pin15), .pin14(ic74245_11_a0[5]), .pin13(ic74245_11_a0[4]),
    .pin12(n74377_3_pin12), .pin11(CLK));
  IC74245 ic74245_15 (
    .DIR(1'b0), .iOE(1'b0), .B0(n74377_3_pin2), .B1(n74377_3_pin5), .B2(n74377_3_pin6), .B3(n74377_3_pin9),
    .B4(n74377_3_pin12), .B5(n74377_3_pin15), .B6(n74377_3_pin16), .B7(n74377_3_pin19), .A0(ALO[0]),
    .A1(ALO[1]), .A2(ALO[2]), .A3(ALO[3]), .A4(ALO[4]), .A5(ALO[5]), .A6(ALO[6]), .A7(ALO[7]));
  LedBar ledbar_5 (
    .led0(ic74245_17_a0[7]), .led1(ic74245_17_a0[6]), .led2(ic74245_17_a0[5]), .led3(ic74245_17_a0[4]),
    .led4(ic74245_17_a0[3]), .led5(ic74245_17_a0[2]), .led6(ic74245_17_a0[1]), .led7(ic74245_17_a0[0]));
  IC74245 ic74245_16 (
    .DIR(1'b0), .iOE(n7414_2_pin6), .B0(n74377_3_pin2), .B1(n74377_3_pin5), .B2(n74377_3_pin6),
    .B3(n74377_3_pin9), .B4(n74377_3_pin12), .B5(n74377_3_pin15), .B6(n74377_3_pin16), .B7(n74377_3_pin19),
    .A0(ic74245_11_a0[0]), .A1(ic74245_11_a0[1]), .A2(ic74245_11_a0[2]), .A3(ic74245_11_a0[3]),
    .A4(ic74245_11_a0[4]), .A5(ic74245_11_a0[5]), .A6(ic74245_11_a0[6]), .A7(ic74245_11_a0[7]));
  IC74245 ic74245_17 (
    .DIR(1'b0), .iOE(1'b0), .B0(n74377_3_pin2), .B1(n74377_3_pin5), .B2(n74377_3_pin6), .B3(n74377_3_pin9),
    .B4(n74377_3_pin12), .B5(n74377_3_pin15), .B6(n74377_3_pin16), .B7(n74377_3_pin19),
    .A0(ic74245_17_a0[0]), .A1(ic74245_17_a0[1]), .A2(ic74245_17_a0[2]), .A3(ic74245_17_a0[3]),
    .A4(ic74245_17_a0[4]), .A5(ic74245_17_a0[5]), .A6(ic74245_17_a0[6]), .A7(ic74245_17_a0[7]));
  _74377 u_74377_4 (
    .pin1(n7414_2_pin8), .pin2(n74377_4_pin2), .pin3(ic74245_11_a0[0]), .pin4(ic74245_11_a0[1]),
    .pin5(n74377_4_pin5), .pin6(n74377_4_pin6), .pin7(ic74245_11_a0[2]), .pin8(ic74245_11_a0[3]),
    .pin9(n74377_4_pin9), .pin19(n74377_4_pin19), .pin18(ic74245_11_a0[7]), .pin17(ic74245_11_a0[6]),
    .pin16(n74377_4_pin16), .pin15(n74377_4_pin15), .pin14(ic74245_11_a0[5]), .pin13(ic74245_11_a0[4]),
    .pin12(n74377_4_pin12), .pin11(CLK));
  IC74245 ic74245_18 (
    .DIR(1'b0), .iOE(1'b0), .B0(n74377_4_pin2), .B1(n74377_4_pin5), .B2(n74377_4_pin6), .B3(n74377_4_pin9),
    .B4(n74377_4_pin12), .B5(n74377_4_pin15), .B6(n74377_4_pin16), .B7(n74377_4_pin19), .A0(BLO[0]),
    .A1(BLO[1]), .A2(BLO[2]), .A3(BLO[3]), .A4(BLO[4]), .A5(BLO[5]), .A6(BLO[6]), .A7(BLO[7]));
  LedBar ledbar_6 (
    .led0(ic74245_20_a0[7]), .led1(ic74245_20_a0[6]), .led2(ic74245_20_a0[5]), .led3(ic74245_20_a0[4]),
    .led4(ic74245_20_a0[3]), .led5(ic74245_20_a0[2]), .led6(ic74245_20_a0[1]), .led7(ic74245_20_a0[0]));
  IC74245 ic74245_19 (
    .DIR(1'b0), .iOE(n7414_2_pin4), .B0(n74377_4_pin2), .B1(n74377_4_pin5), .B2(n74377_4_pin6),
    .B3(n74377_4_pin9), .B4(n74377_4_pin12), .B5(n74377_4_pin15), .B6(n74377_4_pin16), .B7(n74377_4_pin19),
    .A0(ic74245_11_a0[0]), .A1(ic74245_11_a0[1]), .A2(ic74245_11_a0[2]), .A3(ic74245_11_a0[3]),
    .A4(ic74245_11_a0[4]), .A5(ic74245_11_a0[5]), .A6(ic74245_11_a0[6]), .A7(ic74245_11_a0[7]));
  IC74245 ic74245_20 (
    .DIR(1'b0), .iOE(1'b0), .B0(n74377_4_pin2), .B1(n74377_4_pin5), .B2(n74377_4_pin6), .B3(n74377_4_pin9),
    .B4(n74377_4_pin12), .B5(n74377_4_pin15), .B6(n74377_4_pin16), .B7(n74377_4_pin19),
    .A0(ic74245_20_a0[0]), .A1(ic74245_20_a0[1]), .A2(ic74245_20_a0[2]), .A3(ic74245_20_a0[3]),
    .A4(ic74245_20_a0[4]), .A5(ic74245_20_a0[5]), .A6(ic74245_20_a0[6]), .A7(ic74245_20_a0[7]));
  // also tied to GND on the sheet: {n7432_1_pin13, n7432_2_pin13, n7432_1_pin12, n7432_2_pin12, n7408_1_pin1, n7408_1_pin2, n7408_1_pin4, n7408_1_pin5, n7414_2_pin13}

  // Notes on the sheet:
  //   BHO: pull=up
  //   CLK: pull=up
  //   Standalone: pull=up
  //   BHLE: pull=up
  //   AHLE: pull=up
  //   IBHIOE: pull=up
  //   BHOE: pull=up
  //   AHOE: pull=up
  //   EDB: pull=up
  //   ALO: pull=up
  //   EDBIE: pull=up
  //   BLO: pull=up
  //   BLLE: pull=up
  //   ALLE: pull=up
  //   IBLIOE: pull=up
  //   BLOE: pull=up
  //   ALOE: pull=up
  //   AHO: pull=up
  //   AH
  //   BH
  //   AL
  //   BL
endmodule
